# Fritzing sketch air_quality_box (saved by Fritzing 0.9.3b)

parts:
  U1 = ESP8266 NodeMCU LoLin base
  TD-er1 = MH-Z19 CO2 sensor [part_number=MH-Z19]
  DHT1 = DHT22 Humidity and Temperature Sensor
  R1 = Resistor [tolerance=±5% resistance=10k package=THT]
  J2 = female pin header, 4 pins [form="♀ (female)"]
  J4 = female pin header, 7 pins [form="♀ (female)"]

nets:
  GND: U1.GND1-0, U1.GND1-1, U1.GND3-3, U1.GND8-4, U1.GND8-5, TD-er1.GND, DHT1.GND, J2.pin4, J4.pin5
  N1: U1.3V1-0, U1.3V1-1, U1.3V2-0, U1.3V2-1, DHT1.VDD, R1.Pin_1, J2.pin3
  N2: U1.D0-0, U1.D0-3, U1.RST
  N3: U1.D1-0, U1.D1-2, J2.pin1
  N4: U1.D2-0, U1.D2-2, DHT1.DATA, R1.Pin_0
  N5: U1.D3-0, U1.D3-2, TD-er1.RX
  N6: U1.D5-0, U1.D5-3, J4.pin6
  N7: U1.D6-0, U1.D6-2, J4.pin7
  N8: U1.D7-0, U1.D7-3, J2.pin2
  N9: U1.D8-0, U1.D8-3, TD-er1.TX
  VIN: U1.VIN, U1.5V-0, U1.5V-1, U1.5V-2, TD-er1.Vin, J4.pin3

notes:
  GND
  VCC
  SDA
  SCL
  Grove Multiigas Sensor
  Grove multigas sensor (I2C)
  MHZ-19 (UART)
  DHT22
  (One-wire)
  PM10 - analog
  PM2.5 - analog
  NC
  SDS011
  Rx
  Tx
  SDS011 (UART)

custom parts:
  ESP8266 NodeMCU LoLin base: ESP8266 based NodeMCU Base
